# Fritzing sketch EV3_to_Arduino (saved by Fritzing 0.8.7b)
breadboards: 1

parts:
  Parte1 = Arduino Uno (Rev3)
  U1 = XPORT [package=xport]

nets:
  N1: Parte1.A4/SDA, U1.DTR
  N2: Parte1.A5/SCL, U1.CTS

notes:
  Notes to connect EV3 with Arduino One using a I2C Connection
